// Logisim project my_own_computer.circ as structural Verilog
module my_computer (
  input  [15:0] in_1,
  input  in_2,
  input  in_3,
  input  in_4,
  input  in_5,
  input  in_6,
  input  in_7,
  input  in_8,
  input  in_9,
  input  in_10,
  input  in_11,
  output [15:0] out_12
);

  wire [15:0] IR_o, MAR_o, PCAR_o, ram_1_dout, rom_1_data;

  assign out_12 = in_2 ? in_1 : 16'bz;  // Controlled_Buffer controlled_buffer_1
  assign out_12 = in_4 ? 16'h1 : 16'bz;  // Controlled_Buffer controlled_buffer_2
  my_reg D (.i(out_12), .s(in_6), .e(in_7), .o(out_12));
  my_reg JR (.i(out_12), .o(out_12));  // open: s, e
  my_reg R0 (.i(out_12), .o(out_12));  // open: s, e
  my_reg R1 (.i(out_12), .o(out_12));  // open: s, e
  my_reg R2 (.i(out_12), .o(out_12));  // open: s, e
  my_reg IR (.i(out_12), .s(in_11), .e(1'b1), .o(IR_o));
  Controlled_Buffer #(.width(16)) controlled_buffer_3 (.in(IR_o), .out(out_12));  // open: en
  RAM #(.addrWidth(16), .dataWidth(16), .trigger("high")) ram_1 (
    .addr(MAR_o), .we(in_5), .oe(1'b1), .din(out_12), .dout(ram_1_dout));
  ROM #(.addrWidth(16), .dataWidth(16)) rom_1 (.addr(PCAR_o), .data(rom_1_data));
  assign out_12 = in_8 ? ram_1_dout : 16'bz;  // Controlled_Buffer controlled_buffer_4
  assign out_12 = in_10 ? rom_1_data : 16'bz;  // Controlled_Buffer controlled_buffer_5
  my_reg MAR (.i(out_12), .s(in_3), .e(1'b1), .o(MAR_o));
  my_reg PCAR (.i(out_12), .s(in_9), .e(1'b1), .o(PCAR_o));
endmodule

module my_reg (
  input  [15:0] i,
  input  s,
  input  e,
  output [15:0] o
);

  wire [15:0] register_1_q;

  Register #(.trigger("high"), .width(16)) register_1 (.D(i), .clk(s), .Q(register_1_q));  // open: en, clr
  assign o = e ? register_1_q : 16'bz;  // Controlled_Buffer controlled_buffer_1
endmodule
